# Fritzing sketch footMouse (saved by Fritzing 0.9.0b)

parts:
  Pro_Micro1 = Pro Micro
  Componente1 = Thumb Joystick
  Componente2 = Thumb Joystick
  S2 = Round Pushbutton
  S3 = Round Pushbutton

nets:
  N1: Pro_Micro1.GND#3, S2.leg1, S3.leg1
  N2: Pro_Micro1.D3, S3.leg0
  N3: Pro_Micro1.D4, S2.leg0
  N4: Pro_Micro1.D15/SCLK, Componente1.SEL
  N5: Pro_Micro1.D18/A0, Componente1.VERT
  N6: Pro_Micro1.D19/A1, Componente1.HORZ
  N7: Pro_Micro1.D20/A2, Componente2.VERT
  VCC: Pro_Micro1.VCC, Componente1.VCC, Componente2.VCC
  GND: Pro_Micro1.GND#23, Componente1.GND, Componente2.GND, Componente2.SEL

custom parts:
  Pro Micro: The SparkFun Pro Micro is a complete USB-based microcontoller development system, in a very small footprint, capable of implementing many types of projects. All programming can be done via the USB port.
